# Fritzing sketch Sketch (saved by Fritzing 0.9.3b)
breadboards: 1

parts:
  Part1 = Arduino Uno (Rev3) - ICSP
  LED1 = LED - 3mm [color="Red (633nm)" package="3 mm [THT]"]
  R1 = Resistor [tolerance=±5% resistance=220 package="0805 [SMD]"]
  S1 = Pushbutton [package="[SMD]"]
  R2 = Resistor [tolerance=±5% resistance=220 package="0402 [SMD]"]

nets:
  N1: Part1.D2, S1.Pin_1, S1.Pin_2, R2.Pin_1
  N2: Part1.D7, R1.Pin_1
  N3: Part1.5V, S1.Pin_3, S1.Pin_4
  N4: Part1.GND, LED1.cathode, R2.Pin_0
  N5: LED1.anode, R1.Pin_0
